# Fritzing sketch NE555_astabil (saved by Fritzing 0.9.2b)
circuit board: 4cm x 3.5cm
breadboards: 1

parts:
  IC1 = General purpose bipolar Timer [package=dil-08]
  D1 = Rectifier Diode [part_number=1N4001 package="300 mil [THT]"]
  LED1 = LED - 5mm [color="Red (633nm)" package="5 mm [THT]"]
  R1 = Resistor [tolerance=±5% resistance=220 package=THT]
  J1 = female pin header, 4 pins [form="♀ (female)"]
  C1 = Tantalum Capacitor [capacitance=10nF package="200 mil [THT, tantalum]"]
  C2 = Ceramic Capacitor [capacitance=10nF package="200 mil [THT, multilayer]"]
  R3 = TRIMPOT [package=trim_pot_pth]
  R4 = TRIMPOT [package=trim_pot_pth]

nets:
  N1: IC1.GND, LED1.cathode, J1.pin2, J1.pin4, C1.-, C2.0
  N2: IC1.TRI, IC1.TRE, D1.anode, C1.+, R3.CCW, R3.WIPER, R3.CW
  N3: IC1.OUT, R1.Pin_1, J1.pin3
  N4: IC1._RES, IC1.VCC+, J1.pin1, R4.CCW
  N5: IC1.CON, C2.1
  N6: LED1.anode, R1.Pin_0
  N7: R4.WIPER, R4.CW

notes:
  NE555 Timer
  erfindergarden
  GND
  OUT
  VCC

custom parts:
  TRIMPOT: Various small potentiometers for set-and-forget applications
